# Fritzing sketch Demo (saved by Fritzing 0.8.5b)
breadboards: 1

parts:
  Voltmeter1 = Voltmeter
  Ohmmeter1 = Ohmmeter
  Amperemeter1 = Amperemeter
  R1 = Resistor [tolerance=±5% resistance=220 package=THT]
  V1 = DC Power [voltage=5]  # not connected
  LED1 = LED - 5mm [color="Red (633nm)" package="5 mm [THT]"]

nets (from the breadboard view):
  N1: Voltmeter1.Positive, R1.Pin_0
  N2: Voltmeter1.Com, Ohmmeter1.Com, Amperemeter1.Com, LED1.cathode
  N3: Ohmmeter1.Positive, Amperemeter1.Positive, R1.Pin_1, LED1.anode

custom parts:
  Voltmeter: A Standard Multimeter in Current mode
  Ohmmeter: A Standard Multimeter in Current mode
  Amperemeter: A Standard Multimeter in Current mode
